// Logisim project main.circ as structural Verilog: 4 circuits, main circuit ISA
module ULA (
  input  [11:0] A,
  input  [11:0] B,
  input  [2:0] ULAx,
  output [11:0] S,
  output ZERO
);

  wire [3:0] bit_extender_1_out;
  wire [11:0] adder_1_out, and_1_out, divider_1_out, multiplier_1_out, or_1_out, shifter_1_out,
       subtractor_1_out, xor_1_out;

  Bit_Extender #(.in_width(12), .out_width(4)) bit_extender_1 (.in(B), .out(bit_extender_1_out));
  Adder #(.width(12)) adder_1 (.a(A), .b(B), .out(adder_1_out));  // open: cin, cout
  Subtractor #(.width(12)) subtractor_1 (.a(A), .b(B), .out(subtractor_1_out));  // open: bin, bout
  Multiplier #(.width(12)) multiplier_1 (.a(A), .b(B), .out(multiplier_1_out));  // open: cin, cout
  Divider #(.width(12)) divider_1 (.a(A), .b(B), .out(divider_1_out));  // open: upper, rem
  Shifter #(.width(12)) shifter_1 (.in(A), .\dist (bit_extender_1_out), .out(shifter_1_out));
  assign and_1_out = A & B;  // AND_Gate and_1, 12 bits wide
  assign or_1_out = A | B;  // OR_Gate or_1, 12 bits wide
  assign xor_1_out = A ^ B;  // XOR_Gate xor_1, 12 bits wide
  Multiplexer #(.select(3), .width(12)) multiplexer_1 (
    .in0(adder_1_out), .in1(subtractor_1_out), .in2(multiplier_1_out), .in3(divider_1_out),
    .in4(shifter_1_out), .in5(and_1_out), .in6(or_1_out), .in7(xor_1_out), .out(S), .sel(ULAx));
  Comparator #(.width(12)) comparator_1 (.a(S), .b({12{1'b0}}), .eq(ZERO));  // open: gt, lt
endmodule

module BancoRegistradores (
  input  [11:0] D,
  input  CLK,
  input  [3:0] X,
  input  [3:0] RD,
  input  [3:0] Y,
  input  W,
  output [11:0] A,
  output [11:0] B
);

  wire undriven, undriven_2, undriven_3, undriven_4, undriven_5, undriven_6, undriven_7, undriven_8,
       undriven_9, undriven_10, undriven_11, undriven_12, undriven_13, undriven_14, undriven_15, undriven_16;
  wire [11:0] R0, R1, R2, R3, R4, R5, R6, R7, R8, R9, R10, R11, R12, R13, R14, R15;

  Multiplexer #(.select(4)) multiplexer_1 (
    .in0(undriven_7), .in1(undriven_13), .in2(undriven_8), .in3(undriven_9), .in4(undriven_10),
    .in5(undriven_14), .in6(undriven_11), .in7(undriven_12), .in8(undriven), .in9(undriven_15),
    .in10(undriven_2), .in11(undriven_3), .in12(undriven_4), .in13(undriven_16), .in14(undriven_5),
    .in15(undriven_6), .out(W), .sel(RD));
  Register #(.width(12)) register_1 (.D({12{1'b0}}), .en(undriven_7), .clk(CLK), .Q(R0));  // open: clr
  Register #(.width(12)) register_2 (.D(D), .en(undriven_10), .clk(CLK), .Q(R4));  // open: clr
  Register #(.width(12)) register_3 (.D(D), .en(undriven), .clk(CLK), .Q(R8));  // open: clr
  Register #(.width(12)) register_4 (.D(D), .en(undriven_4), .clk(CLK), .Q(R12));  // open: clr
  Register #(.width(12)) register_5 (.D(D), .en(undriven_13), .clk(CLK), .Q(R1));  // open: clr
  Register #(.width(12)) register_6 (.D(D), .en(undriven_14), .clk(CLK), .Q(R5));  // open: clr
  Register #(.width(12)) register_7 (.D(D), .en(undriven_15), .clk(CLK), .Q(R9));  // open: clr
  Register #(.width(12)) register_8 (.D(D), .en(undriven_16), .clk(CLK), .Q(R13));  // open: clr
  Register #(.width(12)) register_9 (.D(D), .en(undriven_8), .clk(CLK), .Q(R2));  // open: clr
  Register #(.width(12)) register_10 (.D(D), .en(undriven_11), .clk(CLK), .Q(R6));  // open: clr
  Register #(.width(12)) register_11 (.D(D), .en(undriven_2), .clk(CLK), .Q(R10));  // open: clr
  Register #(.width(12)) register_12 (.D(D), .en(undriven_5), .clk(CLK), .Q(R14));  // open: clr
  Register #(.width(12)) register_13 (.D(D), .en(undriven_9), .clk(CLK), .Q(R3));  // open: clr
  Register #(.width(12)) register_14 (.D(D), .en(undriven_12), .clk(CLK), .Q(R7));  // open: clr
  Register #(.width(12)) register_15 (.D(D), .en(undriven_3), .clk(CLK), .Q(R11));  // open: clr
  Register #(.width(12)) register_16 (.D(D), .en(undriven_6), .clk(CLK), .Q(R15));  // open: clr
  Multiplexer #(.select(4), .width(12)) multiplexer_2 (
    .in0(R0), .in1(R1), .in2(R2), .in3(R3), .in4(R4), .in5(R5), .in6(R6), .in7(R7), .in8(R8), .in9(R9),
    .in10(R10), .in11(R11), .in12(R12), .in13(R13), .in14(R14), .in15(R15), .out(A), .sel(X));
  Multiplexer #(.select(4), .width(12)) multiplexer_3 (
    .in0(R0), .in1(R1), .in2(R2), .in3(R3), .in4(R4), .in5(R5), .in6(R6), .in7(R7), .in8(R8), .in9(R9),
    .in10(R10), .in11(R11), .in12(R12), .in13(R13), .in14(R14), .in15(R15), .out(B));  // open: sel
endmodule

module ISA (
  output [11:0] EBREAK
);

  wire and_1_out, BGE, BLT, BRC, BRCt, Bx, CLK, comparator_1_eq, comparator_1_gt, Dx, multiplexer_1_out,
       multiplexer_2_out, wBR, wRAM, wRB, ZERO;
  wire [1:0] PCx;
  wire [2:0] ULAx;
  wire [3:0] rom_1_data, rom_1_data_2, rom_1_data_3;
  wire [11:0] A, B, IMM, multiplexer_3_out, multiplexer_4_out, pc_1_out_6, ram_1_dout, ula_1_s;

  Multiplexer multiplexer_1 (.in0(BGE), .in1(BLT), .out(multiplexer_1_out), .sel(BRCt));
  Multiplexer multiplexer_2 (.in0(1'b0), .in1(multiplexer_1_out), .out(multiplexer_2_out), .sel(BRC));
  or or_1 (BGE, comparator_1_gt, comparator_1_eq);
  Comparator #(.width(12)) comparator_1 (.a(A), .b(B), .gt(comparator_1_gt), .eq(comparator_1_eq), .lt(BLT));
  // Probe on pc_1_out_6
  PC pc_1 (.CLK(CLK), .IMM(IMM), .PCx(PCx), .BRANCH(multiplexer_2_out), .A(A), .out_6(pc_1_out_6));
  ROM #(.addrWidth(12), .dataWidth(12)) rom_1 (.addr(pc_1_out_6), .data({rom_1_data_3, rom_1_data_2, rom_1_data}));
  Clock u_CLK (.out(CLK));
  ROM #(.addrWidth(4), .dataWidth(11)) UC (.addr(rom_1_data_3), .data({BRCt, ULAx, wRAM, Dx, Bx, wRB, BRC, PCx}));
  assign IMM = {{8{rom_1_data_2[3]}}, rom_1_data_2};  // Bit_Extender bit_extender_1
  and and_1 (and_1_out, ~BRCt, ~ULAx[2], ~ULAx[1], ~ULAx[0], ~wRAM, ~Dx, ~Bx, ~wRB, ~BRC, ~PCx[1], ~PCx[0]);  // AND_Gate
  assign EBREAK = {{11{and_1_out}}, and_1_out};  // Bit_Extender bit_extender_2
  BancoRegistradores bancoregistradores_1 (
    .D(multiplexer_4_out), .CLK(CLK), .X(rom_1_data), .RD(rom_1_data), .Y(rom_1_data_2), .W(wBR), .A(A), .B(B));
  Multiplexer #(.width(12)) multiplexer_3 (.in0(B), .in1(IMM), .out(multiplexer_3_out), .sel(Bx));
  Multiplexer #(.width(12)) multiplexer_4 (.in0(ula_1_s), .in1(ram_1_dout), .out(multiplexer_4_out), .sel(Dx));
  // Probe on ula_1_s
  ULA ula_1 (.A(A), .B(multiplexer_3_out), .ULAx(ULAx), .S(ula_1_s), .ZERO(ZERO));
  RAM #(.addrWidth(12), .dataWidth(12)) ram_1 (.addr(B), .we(wRAM), .oe(1'b1), .clk(CLK), .din(A), .dout(ram_1_dout));

  // Notes on the sheet:
  //   contents of rom_1 (hex, n*v repeats v):
  //   835 842 253 354 450 553 653 753 d32 850 c02 850 863 a60 8c0 c6 b07 87c a71 f00 82f a10 82f ac0 83c
  //   851 143 e43 8c1 c04 8c4 b0a 2c3 9c1 821 910 821 c10
  //   contents of UC (hex, n*v repeats v):
  //   80 82 84 86 88 8a 8c 8e c0 a0 10 200 600 500 501
endmodule

module PC (
  input  CLK,
  input  [11:0] IMM,
  input  [1:0] PCx,
  input  BRANCH,
  input  [11:0] A,
  output [11:0] out_6
);

  wire [11:0] adder_1_out, adder_2_out, adder_3_out, multiplexer_1_out, multiplexer_2_out;

  Adder #(.width(12)) adder_1 (.a(out_6), .b(IMM), .out(adder_1_out));  // open: cin, cout
  Adder #(.width(12)) adder_2 (.a(IMM), .b(A), .out(adder_2_out));  // open: cin, cout
  Adder #(.width(12)) adder_3 (.a(out_6), .b(12'h1), .out(adder_3_out));  // open: cin, cout
  Multiplexer #(.width(12)) multiplexer_1 (.in0(adder_3_out), .in1(IMM), .out(multiplexer_1_out), .sel(BRANCH));
  Multiplexer #(.select(2), .width(12)) multiplexer_2 (
    .in0(adder_3_out), .in1(adder_1_out), .in2(multiplexer_1_out), .in3(adder_2_out),
    .out(multiplexer_2_out), .sel(PCx));
  Register #(.width(12)) register_1 (.D(multiplexer_2_out), .en(1'b1), .clk(CLK), .Q(out_6));  // open: clr

  // Notes on the sheet:
  //   PC + IMM
  //   PC + 1
  //   BRANCH
  //   1. PC + 1
  //   2. PC + IMM
  //   3. BRANCH
  //   4. JALR
endmodule
